# Fritzing sketch Microscope (saved by Fritzing 0.7.0b)
breadboards: 2

parts:
  Arduino1 = Arduino
  Part1 = EasyDriver_v44
  Part2 = EasyDriver_v44
  Part3 = EasyDriver_v44
  R1 = Rotary Potentiometer (Small) [maximum_resistance=100kΩ]
  R2 = Rotary Potentiometer (Small) [maximum_resistance=100kΩ]
  R3 = Rotary Potentiometer (Small) [maximum_resistance=100kΩ]
  M1 = Stepper Motor - Bipolar
  M2 = Stepper Motor - Bipolar
  M3 = Stepper Motor - Bipolar
  Power_plug1 = Power plug  # not connected
  U1 = Voltage Regulator - 5V [package="TO220 [THT]"]

nets:
  N1: Arduino1.D10, Part1.STEP
  N2: Arduino1.D9, Part2.STEP
  N3: Arduino1.D8, Part1.DIR
  N4: Arduino1.D7, Part2.DIR
  N5: Arduino1.D6, Part3.DIR
  N6: Arduino1.D5, Part1.SLEEP, Part2.SLEEP, Part3.SLEEP
  N7: Arduino1.D4, Part1.ENABLE, Part2.ENABLE, Part3.ENABLE
  N8: Arduino1.D3, Part3.STEP
  N9: Arduino1.D2, Part2.RESET, Part3.RESET
  N10: Arduino1.A0, R1.wiper
  N11: Arduino1.A1, R3.wiper
  N12: Arduino1.A2, R2.wiper
  GND: Part1.GND, Part2.GND, Part3.GND, R1.leg1, R1.leg2, R2.leg1, R2.leg2, R3.leg1, R3.leg2, U1.input_voltage, U1.GND, U1.output_voltage
  N13: Part1.V+, Part2.V+, Part3.V+
  N14: Part1.OUT2A, M1.A
  N15: Part1.OUT2B, M1.C
  N16: Part1.OUT1A, M1.B
  N17: Part1.OUT1B, M1.D
  N18: Part2.OUT2A, M2.A
  N19: Part2.OUT2B, M2.C
  N20: Part2.OUT1A, M2.B
  N21: Part2.OUT1B, M2.D
  N22: Part3.OUT2A, M3.A
  N23: Part3.OUT2B, M3.C
  N24: Part3.OUT1A, M3.B
  N25: Part3.OUT1B, M3.D
